// Logisim project 流水线框图.circ as structural Verilog: 29 circuits, main circuit main
module main (
  input  [7:0] INTERRUPTIONS,
  input  CLK,
  input  RST
);

  wire alu_1_out_5, alu_1_out_6, alu_1_out_7, control_unit_cu_exmem_flush, control_unit_cu_exmem_stall,
       control_unit_cu_idex_flush, control_unit_cu_idex_stall, control_unit_cu_ifid_flush,
       control_unit_cu_ifid_stall, control_unit_cu_pc_stall, control_unit_out_23, control_unit_out_28,
       cpu_interface_1_mem_stall, decoder_p3, decoder_p4, decoder_p5, decoder_p6, decoder_p7, decoder_p9,
       decoder_p12, decoder_p16, decoder_p18, decoder_p19, decoder_p20, decoder_p21, decoder_p23,
       decoder_p24, decoder_p25, decoder_p26, decoder_p28, decoder_p31, except_detect1_1_out_4,
       except_detect2_1_out_8, EXMEM_cp0_w_en_2, EXMEM_exmem_branch, EXMEM_exmem_lf, EXMEM_exmem_mem_r,
       EXMEM_exmem_nen_w, EXMEM_exmem_reg_w, EXMEM_exmem_zf, EXMEM_out_55, EXMEM_out_56, idex_reg_ex_jmp,
       idex_reg_ex_jr, idex_reg_ex_nop, idex_reg_idex_b_sel, idex_reg_idex_branch, idex_reg_idex_cp0_w_en,
       idex_reg_idex_eret, idex_reg_idex_mem_r, idex_reg_idex_mem_w, idex_reg_idex_movnz, idex_reg_idex_movz,
       idex_reg_idex_of_w_disen, idex_reg_idex_reg_w, idex_reg_idex_shamt_sel, idex_reg_idex_syscall,
       idex_reg_out_71, idex_reg_out_73, idex_reg_out_74, ifid_reg_id_nop, is_delayslot_out_4,
       memwb_reg_1_memwb_cp0_w_en, memwb_reg_1_memwb_mem_r, memwb_reg_1_memwb_reg_w, mul_div_md_stall,
       not_1_out, or_1_out, or_2_out, reg_w_gen_1_out_7, undriven_2;
  wire [1:0] decoder_p13, decoder_p29, decoder_p30, forwarding_unit_1_a_sel_1_0,
       forwarding_unit_1_b_sel_31_0, idex_reg_idex_exres_sel, idex_reg_idex_shift_op_1_0;
  wire [2:0] control_unit_cu_pc_src_2_0, decoder_p8, decoder_p10, decoder_p14, decoder_p15, decoder_p22,
       EXMEM_exmem_condition_2_0, EXMEM_exmem_load_sel_2_0, idex_reg_idex_conition_2_0,
       idex_reg_idex_load_sel_2_0, idex_reg_idex_store_sel_2_0;
  wire [3:0] decoder_p27, EXMEM_mem_byte_w_en, EXMEM_reg_byte_w_en_3_0_2, idex_reg_idex_alu_op_3_0,
       idex_reg_idex_md_op_3_0_2, load_b_w_e_gen_b_w_en_3_0, memwb_reg_1_reg_byte_w_en_3_0_2,
       store_b_w_e_gen_b_w_en_3_0;
  wire [4:0] decoder_p2, decoder_p11, decoder_p17, EXMEM_exmem_cp0_dst_addr_4_0, EXMEM_exmem_rd_addr_4_0,
       idex_reg_idex_cp0_addr_4_0, idex_reg_idex_rd_addr_4_0, idex_reg_idex_rs_addr_4_0,
       idex_reg_idex_rt_addr_4_0, idex_reg_idex_shamt_4_0, ifid_reg_ifid_rd_addr_4_0,
       ifid_reg_ifid_rs_addr_4_0, ifid_reg_ifid_rt_addr_4_0, memwb_reg_1_memwb_cp0_dst_addr_4_0,
       memwb_reg_1_memwb_rd_addr_4_0, multiplexer_2_out, multiplexer_4_out, multiplexer_9_out;
  wire [15:0] ifid_reg_ifid_imm_15_0;
  wire [31:0] adder_1_out, adder_2_out, alu_1_out_4, barrel_shifter_1_shift_out_31_0,
       control_unit_cu_vector_31_0, cp0_1_cause_o_31_0, cp0_1_data_o_31_0, cp0_1_epc_o_31_0,
       cp0_1_status_o_31_0, cpu_interface_1_dc_data_out, cpu_interface_1_ic_data_out,
       EXMEM_exmem_alu_res_31_0, EXMEM_exmem_pc_4_31_0, EXMEM_exmem_pc_31_0, EXMEM_exmem_rt_data_31_0,
       EXMEM_exmem_target_31_0, final_target_1_final_target_31_0, forwarding_unit_1_input_a_31_0,
       forwarding_unit_1_input_b_31_0, GPR_rs_data_31_0, GPR_rt_data_31_0, idex_reg_idex_imm_ext_31_0,
       idex_reg_idex_op_a_31_0, idex_reg_idex_op_b_31_0, idex_reg_idex_pc_4_31_0, idex_reg_idex_pc_31_0,
       ifid_reg_ifid_instr_31_0, ifid_reg_ifid_jump_instr_31_0, ifid_reg_ifid_pc_4_31_0,
       ifid_reg_ifid_pc_31_0, interrupt_except_handle_1_out_4, load_shifter_out_4,
       memwb_reg_1_memwb_exdata_31_0, memwb_reg_1_memwb_memdata_31_0, mul_div_res_out_31_0,
       multiplexer_1_out, multiplexer_3_out, multiplexer_5_out, multiplexer_6_out, multiplexer_7_out,
       multiplexer_8_out, multiplexer_10_out, multiplexer_11_out, multiplexer_12_out, PC_pc_out_31_0,
       store_shifter_real_rt_data_31_0, undriven, \位扩展单元_imm_ext_31_0 ;

  Multiplexer #(.select(3), .width(32), .disabled(0), .enable("false")) multiplexer_1 (
    .in0(ifid_reg_ifid_jump_instr_31_0), .in1(control_unit_cu_vector_31_0), .in2(cp0_1_epc_o_31_0),
    .in3(final_target_1_final_target_31_0), .in4(adder_1_out), .out(multiplexer_1_out),
    .sel(control_unit_cu_pc_src_2_0));  // open: in5, in6, in7
  pc PC (
    .stall(control_unit_cu_pc_stall), .clk(CLK), .reset(RST), .pc_out_31_0(PC_pc_out_31_0),
    .pc_in_31_0(multiplexer_1_out));
  cpu_interface cpu_interface_1 (
    .clk(CLK), .reset(RST), .ic_addr(PC_pc_out_31_0[29:0]), .dc_read_in(EXMEM_exmem_mem_r),
    .dc_write_in(EXMEM_exmem_nen_w), .dc_addr(EXMEM_exmem_alu_res_31_0[31:2]),
    .data_reg(EXMEM_exmem_rt_data_31_0), .dc_byte_w_en(EXMEM_mem_byte_w_en),
    .ic_data_out(cpu_interface_1_ic_data_out), .dc_data_out(cpu_interface_1_dc_data_out),
    .mem_stall(cpu_interface_1_mem_stall));
  ifid_reg ifid_reg (
    .clk(CLK), .reset(RST), .ifid_pc_31_0(ifid_reg_ifid_pc_31_0), .cu_stall(control_unit_cu_ifid_stall),
    .cu_flush(control_unit_cu_ifid_flush), .ifid_rs_addr_4_0(ifid_reg_ifid_rs_addr_4_0),
    .ifid_rt_addr_4_0(ifid_reg_ifid_rt_addr_4_0), .pc_31_0(PC_pc_out_31_0),
    .ifid_rd_addr_4_0(ifid_reg_ifid_rd_addr_4_0), .ifid_imm_15_0(ifid_reg_ifid_imm_15_0),
    .pc_4_31_0(adder_1_out), .ifid_pc_4_31_0(ifid_reg_ifid_pc_4_31_0),
    .instr_31_0(cpu_interface_1_ic_data_out), .ifid_jump_instr_31_0(ifid_reg_ifid_jump_instr_31_0),
    .ifid_instr_31_0(ifid_reg_ifid_instr_31_0), .id_nop(ifid_reg_id_nop));
  Adder #(.width(32)) adder_1 (.a(PC_pc_out_31_0), .b(32'h4), .out(adder_1_out));  // open: cin, cout
  buf or_1 (or_1_out, cpu_interface_1_mem_stall);  // OR_Gate
  // decoder decoder: pin names not known; wires that end beside it: ifid_reg_ifid_instr_31_0, decoder_p2, decoder_p3, decoder_p4, decoder_p5, decoder_p6, decoder_p7, decoder_p8, decoder_p9, decoder_p10, decoder_p11, decoder_p12, decoder_p13, decoder_p14, decoder_p15, decoder_p16, decoder_p17, decoder_p18, decoder_p19, decoder_p20, decoder_p21, decoder_p22, decoder_p23, decoder_p24, decoder_p25, decoder_p26, decoder_p27, decoder_p28, decoder_p29, decoder_p30, decoder_p31
  GPR GPR (
    .clk(not_1_out), .reset(RST), .Rs_data_31_0(GPR_rs_data_31_0), .Rs_addr_4_0(ifid_reg_ifid_rs_addr_4_0),
    .Rt_addr_4_0(multiplexer_2_out), .Rd_addr_4_0(memwb_reg_1_memwb_rd_addr_4_0),
    .Rt_data_31_0(GPR_rt_data_31_0), .write(memwb_reg_1_memwb_reg_w), .data_in_31_0(multiplexer_12_out),
    .Rd_byte_w_en_3_0(memwb_reg_1_reg_byte_w_en_3_0_2));
  not not_1 (not_1_out, CLK);
  Multiplexer #(.width(5), .enable("false")) multiplexer_2 (
    .in0(ifid_reg_ifid_rt_addr_4_0), .in1({5{1'b0}}), .out(multiplexer_2_out), .sel(decoder_p31));
  Multiplexer #(.width(32), .enable("false")) multiplexer_3 (
    .in0(cp0_1_data_o_31_0), .in1(GPR_rt_data_31_0), .out(multiplexer_3_out), .sel(decoder_p28));
  imm_ext \u_位扩展单元  (
    .ifid_imm_15_0(ifid_reg_ifid_imm_15_0), .imm_ext_31_0(\位扩展单元_imm_ext_31_0 ), .id_imm_ext_1_0(decoder_p29));
  except_detect1 except_detect1_1 (
    .in_1(decoder_p19), .in_2(decoder_p20), .in_3(decoder_p26), .out_4(except_detect1_1_out_4));
  Multiplexer #(.select(2), .width(5), .enable("false")) multiplexer_4 (
    .in0(ifid_reg_ifid_rt_addr_4_0), .in1(ifid_reg_ifid_rd_addr_4_0), .in2({5{1'b1}}),
    .out(multiplexer_4_out), .sel(decoder_p30));  // open: in3
  control_unit control_unit (
    .mem_stall(or_1_out), .cu_ifid_flush(control_unit_cu_ifid_flush), .cu_pc_stall(control_unit_cu_pc_stall),
    .cu_idex_stall(control_unit_cu_idex_stall), .id_jmp(decoder_p3),
    .cu_idex_flush(control_unit_cu_idex_flush), .cu_ifid_stall(control_unit_cu_ifid_stall),
    .real_rs_addr_4_0(ifid_reg_ifid_rs_addr_4_0), .real_rd_addr_4_0(idex_reg_idex_rd_addr_4_0),
    .cu_exmem_stall(control_unit_cu_exmem_stall), .cu_exmem_flush(control_unit_cu_exmem_flush),
    .real_rt_addr_4_0(multiplexer_2_out), .cu_vector_31_0(control_unit_cu_vector_31_0),
    .cu_pc_src_2_0(control_unit_cu_pc_src_2_0), .out_25(RST), .out_23(control_unit_out_23),
    .mem_branch_state(undriven_2), .out_28(control_unit_out_28), .in_14(interrupt_except_handle_1_out_4));  // open: preedicted_idex_pc_31_0, exmem_syscall, target_exmem_pc_31_0, id_jr, bpu_write_en, cp0_intr, exmem_eret, cu_cp0_w_en, cu_exec_code_4_0, cu_epc_321_0, idex_mem_r, out_26, out_24
  idex_reg idex_reg (
    .idex_mem_w(idex_reg_idex_mem_w), .idex_mem_r(idex_reg_idex_mem_r), .clk(CLK),
    .idex_reg_w(idex_reg_idex_reg_w), .reset(RST), .idex_branch(idex_reg_idex_branch),
    .cu_stall(control_unit_cu_idex_stall), .idex_conition_2_0(idex_reg_idex_conition_2_0),
    .cu_flush(control_unit_cu_idex_flush), .idex_of_w_disen(idex_reg_idex_of_w_disen),
    .id_rd_addr_4_0(multiplexer_4_out), .idex_exres_sel(idex_reg_idex_exres_sel),
    .idex_B_sel(idex_reg_idex_b_sel), .idex_ALU_op_3_0(idex_reg_idex_alu_op_3_0),
    .ifid_pc_31_0(ifid_reg_ifid_pc_31_0), .idex_shamt_sel(idex_reg_idex_shamt_sel),
    .idex_shift_op_1_0(idex_reg_idex_shift_op_1_0), .idex_shamt_4_0(idex_reg_idex_shamt_4_0),
    .ifid_pc_4_31_0(ifid_reg_ifid_pc_4_31_0), .idex_rs_addr_4_0(idex_reg_idex_rs_addr_4_0),
    .idex_rt_addr_4_0(idex_reg_idex_rt_addr_4_0), .idex_rd_addr_4_0(idex_reg_idex_rd_addr_4_0),
    .gpr_rs_31_0(GPR_rs_data_31_0), .idex_op_A_31_0(idex_reg_idex_op_a_31_0),
    .gpr_rt_31_0(multiplexer_3_out), .idex_op_B_31_0(idex_reg_idex_op_b_31_0),
    .id_imm_ext_31_0(\位扩展单元_imm_ext_31_0 ), .idex_imm_ext_31_0(idex_reg_idex_imm_ext_31_0),
    .idex_pc_31_0(idex_reg_idex_pc_31_0), .idex_pc_4_31_0(idex_reg_idex_pc_4_31_0),
    .idex_load_sel_2_0(idex_reg_idex_load_sel_2_0), .idex_store_sel_2_0(idex_reg_idex_store_sel_2_0),
    .idex_cp0_addr_4_0(idex_reg_idex_cp0_addr_4_0), .idex_syscall(idex_reg_idex_syscall),
    .idex_cp0_w_en(idex_reg_idex_cp0_w_en), .idex_eret(idex_reg_idex_eret), .idex_movz(idex_reg_idex_movz),
    .idex_movnz(idex_reg_idex_movnz), .in_13(decoder_p4), .in_14(decoder_p5), .in_15(decoder_p6),
    .in_19(decoder_p7), .in_24(decoder_p8), .in_28(decoder_p9), .in_16(decoder_p10), .in_20(decoder_p11),
    .in_25(decoder_p12), .in_29(decoder_p13), .in_32(decoder_p14), .in_17(decoder_p15), .in_21(decoder_p16),
    .in_26(decoder_p17), .in_30(decoder_p18), .in_33(decoder_p19), .in_18(decoder_p20), .in_22(decoder_p21),
    .in_27(decoder_p22), .in_31(decoder_p23), .in_34(decoder_p24), .in_12(decoder_p3),
    .in_11(ifid_reg_id_nop), .ex_nop(idex_reg_ex_nop), .ex_jmp(idex_reg_ex_jmp), .ex_jr(idex_reg_ex_jr),
    .in_23(except_detect1_1_out_4), .in_35(decoder_p25), .out_74(idex_reg_out_74), .out_71(idex_reg_out_71),
    .out_73(idex_reg_out_73), .in_37(is_delayslot_out_4), .idex_Md_op_3_0(decoder_p27),
    .idex_Md_op_3_0_2(idex_reg_idex_md_op_3_0_2));  // open: out_72, in_36, out_75, in_38
  or or_2 (or_2_out, idex_reg_idex_movz, idex_reg_idex_movnz);
  is_delayslot is_delayslot (
    .in_1(idex_reg_ex_jmp), .in_2(idex_reg_ex_jr), .in_3(idex_reg_idex_b_sel), .out_4(is_delayslot_out_4));
  forwarding_unit forwarding_unit_1 (
    .rs_data_31_0(idex_reg_idex_op_a_31_0), .rt_data_31_0(idex_reg_idex_op_b_31_0),
    .memwb_byte_en_3_0(memwb_reg_1_reg_byte_w_en_3_0_2), .rs_addr(idex_reg_idex_rs_addr_4_0),
    .rt_addr(idex_reg_idex_rt_addr_4_0), .memwb_rd_addr_4_0(memwb_reg_1_memwb_rd_addr_4_0),
    .input_A_31_0(forwarding_unit_1_input_a_31_0), .input_B_31_0(forwarding_unit_1_input_b_31_0),
    .A_sel_1_0(forwarding_unit_1_a_sel_1_0), .memwb_data_31_0(multiplexer_12_out),
    .B_sel_31_0(forwarding_unit_1_b_sel_31_0), .exmem_rd_addr(EXMEM_exmem_rd_addr_4_0),
    .exmem_byte_en_3_0(EXMEM_reg_byte_w_en_3_0_2));
  Multiplexer #(.select(2), .width(32), .enable("false")) multiplexer_5 (
    .in0(idex_reg_idex_op_a_31_0), .in1(EXMEM_exmem_alu_res_31_0), .in2(forwarding_unit_1_input_a_31_0),
    .out(multiplexer_5_out), .sel(forwarding_unit_1_a_sel_1_0));  // open: in3
  Multiplexer #(.select(2), .width(32), .enable("false")) multiplexer_6 (
    .in0(idex_reg_idex_op_b_31_0), .in1(EXMEM_exmem_alu_res_31_0), .in2(forwarding_unit_1_input_b_31_0),
    .out(multiplexer_6_out), .sel(forwarding_unit_1_b_sel_31_0));  // open: in3
  Multiplexer #(.width(32), .enable("false")) multiplexer_7 (
    .in0(multiplexer_5_out), .in1(undriven), .out(multiplexer_7_out), .sel(or_2_out));
  Multiplexer #(.width(32), .enable("false")) multiplexer_8 (
    .in0(multiplexer_6_out), .in1(idex_reg_idex_imm_ext_31_0), .out(multiplexer_8_out),
    .sel(idex_reg_idex_b_sel));
  Multiplexer #(.width(5), .enable("false")) multiplexer_9 (
    .in0(idex_reg_idex_shamt_4_0), .in1(multiplexer_5_out[4:0]), .out(multiplexer_9_out),
    .sel(idex_reg_idex_shamt_sel));
  except_detect2 except_detect2_1 (
    .in_1(alu_1_out_5), .in_2(alu_1_out_6), .in_3(alu_1_out_7), .in_4(idex_reg_out_73),
    .in_5(idex_reg_idex_of_w_disen), .in_6(idex_reg_out_74), .out_8(except_detect2_1_out_8),
    .in_7(idex_reg_idex_conition_2_0));
  muldiv mul_div (
    .Clk(CLK), .Md_op_31_0(idex_reg_idex_md_op_3_0_2), .Rs_in_31_0(multiplexer_7_out),
    .Rt_in_31_0(multiplexer_8_out), .Res_out_31_0(mul_div_res_out_31_0), .Md_stall(mul_div_md_stall));
  ALU alu_1 (
    .in_2(multiplexer_7_out), .in_3(multiplexer_8_out), .in_1(idex_reg_idex_alu_op_3_0), .out_4(alu_1_out_4),
    .out_5(alu_1_out_5), .out_6(alu_1_out_6), .out_7(alu_1_out_7));
  barrel_shifter barrel_shifter_1 (
    .shift_amount_4_0(multiplexer_9_out), .shift_op_1_0(idex_reg_idex_shift_op_1_0),
    .shift_in_31_0(multiplexer_6_out), .shift_out_31_0(barrel_shifter_1_shift_out_31_0));
  reg_w_gen reg_w_gen_1 (
    .in_3(idex_reg_idex_movz), .in_4(idex_reg_idex_movnz), .in_5(idex_reg_idex_reg_w),
    .in_6(idex_reg_idex_of_w_disen), .out_7(reg_w_gen_1_out_7), .in_1(alu_1_out_7), .in_2(alu_1_out_6));
  Adder #(.width(32)) adder_2 (
    .a({idex_reg_idex_imm_ext_31_0[29:0], 2'b00}), .b(idex_reg_idex_pc_4_31_0), .out(adder_2_out));  // open: cin, cout
  Multiplexer #(.width(32), .disabled(0), .enable("false")) multiplexer_10 (
    .in0(adder_2_out), .in1(alu_1_out_4), .out(multiplexer_10_out), .sel(idex_reg_ex_jr));
  lw_b_w_e_gen load_b_w_e_gen (
    .addr_1_0(alu_1_out_4[1:0]), .load_sel_2_0(idex_reg_idex_load_sel_2_0),
    .b_w_en_3_0(load_b_w_e_gen_b_w_en_3_0));
  sw_b_w_e_gen store_b_w_e_gen (
    .addr_1_0(alu_1_out_4[1:0]), .store_sel_2_0(idex_reg_idex_store_sel_2_0),
    .b_w_en_3_0(store_b_w_e_gen_b_w_en_3_0));
  real_rt_data_gen store_shifter (
    .addr_1_0(alu_1_out_4[1:0]), .store_sel_2_0(idex_reg_idex_store_sel_2_0),
    .rt_data_31_0(multiplexer_6_out), .real_rt_data_31_0(store_shifter_real_rt_data_31_0));
  Multiplexer #(.select(2), .width(32), .enable("false")) multiplexer_11 (
    .in0(alu_1_out_4), .in1(barrel_shifter_1_shift_out_31_0), .in2(multiplexer_10_out),
    .in3(multiplexer_5_out), .out(multiplexer_11_out), .sel(idex_reg_idex_exres_sel));
  exmem_reg EXMEM (
    .clk(CLK), .idex_branch(idex_reg_idex_branch), .reset(RST),
    .idex_condition_2_0(idex_reg_idex_conition_2_0), .cu_stall(control_unit_cu_exmem_stall),
    .cu_flush(control_unit_cu_exmem_flush), .adder_target_31_0(multiplexer_10_out),
    .idex_mem_w(idex_reg_idex_mem_w), .idex_pc_31_0(idex_reg_idex_pc_31_0), .idex_memr(idex_reg_idex_mem_r),
    .idex_pc_4_31_0(idex_reg_idex_pc_4_31_0), .alu_lf(alu_1_out_5), .alu_zf(alu_1_out_6),
    .aligned_rt_data_31_0(store_shifter_real_rt_data_31_0), .ex_res_31_0(multiplexer_11_out),
    .real_rd_addr_4_0(idex_reg_idex_rd_addr_4_0), .idex_load_sel_2_0(idex_reg_idex_load_sel_2_0),
    .exmem_nen_w(EXMEM_exmem_nen_w), .exmem_mem_r(EXMEM_exmem_mem_r), .exmem_reg_w(EXMEM_exmem_reg_w),
    .exmem_condition_2_0(EXMEM_exmem_condition_2_0), .exmem_branch(EXMEM_exmem_branch),
    .exmem_alu_res_31_0(EXMEM_exmem_alu_res_31_0), .exmem_rt_data_31_0(EXMEM_exmem_rt_data_31_0),
    .exmem_target_31_0(EXMEM_exmem_target_31_0), .exmem_lf(EXMEM_exmem_lf), .exmem_zf(EXMEM_exmem_zf),
    .exmem_pc_31_0(EXMEM_exmem_pc_31_0), .exmem_pc_4_31_0(EXMEM_exmem_pc_4_31_0),
    .exmem_rd_addr_4_0(EXMEM_exmem_rd_addr_4_0), .exmem_load_sel_2_0(EXMEM_exmem_load_sel_2_0),
    .reg_byte_w_en_3_0(load_b_w_e_gen_b_w_en_3_0), .mem_byte_w_en_3_0(store_b_w_e_gen_b_w_en_3_0),
    .reg_byte_w_en_3_0_2(EXMEM_reg_byte_w_en_3_0_2), .mem_byte_w_en(EXMEM_mem_byte_w_en),
    .idex_cp0_dst_addr_4_0(idex_reg_idex_cp0_addr_4_0), .cp0_w_en(idex_reg_idex_cp0_w_en),
    .syscall(idex_reg_idex_syscall), .exmem_cp0_dst_addr_4_0(EXMEM_exmem_cp0_dst_addr_4_0),
    .cp0_w_en_2(EXMEM_cp0_w_en_2), .idex_eret(idex_reg_idex_eret), .alu_of(alu_1_out_7),
    .idex_reg_w(reg_w_gen_1_out_7), .ex_nop(idex_reg_ex_nop), .ex_jmp(idex_reg_ex_jmp),
    .mem_jmp(control_unit_out_23), .in_28(idex_reg_out_71), .in_30(except_detect2_1_out_8),
    .out_55(EXMEM_out_55), .out_56(EXMEM_out_56), .in_29(idex_reg_ex_jr));  // open: exmem_store_sel_2_0, syscall_2, exmem_eret, mem_nop, in_31, out_57
  cp0 cp0_1 (
    .w_addr_i_4_0(memwb_reg_1_memwb_cp0_dst_addr_4_0), .is_in_delay_slot(EXMEM_out_55),
    .data_in_31_0(multiplexer_12_out), .excepttype_i_31_0(interrupt_except_handle_1_out_4),
    .data_o_31_0(cp0_1_data_o_31_0), .status_o_31_0(cp0_1_status_o_31_0), .interruption_7_0(INTERRUPTIONS),
    .r_addr_i_4_0(decoder_p2), .current_inst_addr_i_31_0(EXMEM_exmem_pc_31_0),
    .cause_o_31_0(cp0_1_cause_o_31_0), .epc_o_31_0(cp0_1_epc_o_31_0), .w_en_i(memwb_reg_1_memwb_cp0_w_en),
    .clk(CLK), .reset(RST));  // open: time_int_o
  interrupt_except_handle interrupt_except_handle_1 (
    .in_1(cp0_1_status_o_31_0), .in_2(cp0_1_cause_o_31_0), .in_3(EXMEM_out_56),
    .out_4(interrupt_except_handle_1_out_4));
  final_target final_target_1 (
    .exmem_branch(EXMEM_exmem_branch), .exmem_condition_2_0(EXMEM_exmem_condition_2_0),
    .exmem_lf(EXMEM_exmem_lf), .exmem_zf(EXMEM_exmem_zf), .exmem_target_31_0(EXMEM_exmem_target_31_0),
    .exmem_pc_4_31_0(EXMEM_exmem_pc_4_31_0), .final_target_31_0(final_target_1_final_target_31_0),
    .branch_state(undriven_2));
  mem_r_data_shift load_shifter (
    .in_1(EXMEM_exmem_alu_res_31_0[1:0]), .in_2(EXMEM_exmem_load_sel_2_0),
    .in_3(cpu_interface_1_dc_data_out), .out_4(load_shifter_out_4));
  memwb_reg memwb_reg_1 (
    .clk(CLK), .reset(RST), .exmem_mem_r(EXMEM_exmem_mem_r), .exmem_mem_w(EXMEM_exmem_reg_w),
    .exmem_rd_addr_4_0(EXMEM_exmem_rd_addr_4_0), .reg_byte_w_en_3_0(EXMEM_reg_byte_w_en_3_0_2),
    .mem_data_31_0(load_shifter_out_4), .ex_data_31_0(EXMEM_exmem_alu_res_31_0),
    .memwb_mem_r(memwb_reg_1_memwb_mem_r), .memwb_reg_w(memwb_reg_1_memwb_reg_w),
    .memwb_rd_addr_4_0(memwb_reg_1_memwb_rd_addr_4_0), .reg_byte_w_en_3_0_2(memwb_reg_1_reg_byte_w_en_3_0_2),
    .memwb_memdata_31_0(memwb_reg_1_memwb_memdata_31_0), .memwb_exdata_31_0(memwb_reg_1_memwb_exdata_31_0),
    .exmem_cp0_dst_addr_4_0(EXMEM_exmem_cp0_dst_addr_4_0), .exmem_cp0_w_en(EXMEM_cp0_w_en_2),
    .memwb_cp0_dst_addr_4_0(memwb_reg_1_memwb_cp0_dst_addr_4_0), .memwb_cp0_w_en(memwb_reg_1_memwb_cp0_w_en),
    .aligned_rt_data_31_0(EXMEM_exmem_rt_data_31_0), .in_2(control_unit_out_28));  // open: aligned_rt_data_31_0_2, in_1
  Multiplexer #(.width(32), .enable("false")) multiplexer_12 (
    .in0(memwb_reg_1_memwb_memdata_31_0), .in1(memwb_reg_1_memwb_exdata_31_0), .out(multiplexer_12_out),
    .sel(memwb_reg_1_memwb_mem_r));

  // Notes on the sheet:
  //   byte_en
  //   addr
  //   write
  //   data
  //   except_detect1
  //   Rd_addr_sel
  //   new_reg_w = ((movnz && zf) || (movz && !zf) || (id_of_w_disen && of)) ? 0 : idex_reg_w
  //   32'd0
  //   Rt_imm_sel
  //   shift_amount_sel
  //   except_detect2
  //   ALU
  //   Barrel Shifter
  //   Exec_res_sel
endmodule

module ifid_reg (
  input  clk,
  input  reset,
  input  cu_stall,
  input  cu_flush,
  input  [31:0] pc_31_0,
  input  [31:0] pc_4_31_0,
  input  [31:0] instr_31_0,
  output [31:0] ifid_pc_31_0,
  output [31:0] ifid_pc_4_31_0,
  output [31:0] ifid_jump_instr_31_0,
  output [31:0] ifid_instr_31_0,
  output [4:0] ifid_rs_addr_4_0,
  output [4:0] ifid_rt_addr_4_0,
  output [15:0] ifid_imm_15_0,
  output [4:0] ifid_rd_addr_4_0,
  output id_nop
);
endmodule

module decoder (
  input  [31:0] ifid_instr_31_0,
  output out_2,
  output out_3,
  output out_4,
  output [2:0] out_5,
  output out_6,
  output out_7,
  output [2:0] out_8,
  output [4:0] out_9,
  output out_10,
  output [1:0] out_11,
  output [2:0] out_12,
  output [2:0] out_13,
  output out_14,
  output [4:0] out_15,
  output out_16,
  output out_17,
  output out_18,
  output out_19,
  output out_20,
  output out_21,
  output [2:0] out_22,
  output out_23,
  output out_24,
  output [4:0] cp0_src_addr_3_0,
  output id_rt_data_sel,
  output [1:0] id_rd_addr_sel_1_0,
  output id_jump,
  output out_29,
  output [1:0] in_imm_ext_1_0,
  output id_rt_addr_sel,
  output out_32,
  output [3:0] idex_Md_op
);
endmodule

module idex_reg (
  input  clk,
  input  reset,
  input  cu_stall,
  input  cu_flush,
  input  [4:0] id_rd_addr_4_0,
  input  [31:0] ifid_pc_31_0,
  input  [31:0] ifid_pc_4_31_0,
  input  [31:0] gpr_rs_31_0,
  input  [31:0] gpr_rt_31_0,
  input  [31:0] id_imm_ext_31_0,
  input  in_11,
  input  in_12,
  input  in_13,
  input  in_14,
  input  in_15,
  input  [2:0] in_16,
  input  [2:0] in_17,
  input  in_18,
  input  in_19,
  input  [4:0] in_20,
  input  in_21,
  input  in_22,
  input  in_23,
  input  [2:0] in_24,
  input  in_25,
  input  [4:0] in_26,
  input  [2:0] in_27,
  input  in_28,
  input  [1:0] in_29,
  input  in_30,
  input  in_31,
  input  [2:0] in_32,
  input  in_33,
  input  in_34,
  input  in_35,
  input  in_36,
  input  in_37,
  input  in_38,
  input  [3:0] idex_Md_op_3_0,
  output idex_movz,
  output idex_movnz,
  output idex_mem_w,
  output idex_mem_r,
  output idex_reg_w,
  output idex_branch,
  output [2:0] idex_conition_2_0,
  output idex_of_w_disen,
  output [1:0] idex_exres_sel,
  output idex_B_sel,
  output [3:0] idex_ALU_op_3_0,
  output idex_shamt_sel,
  output [4:0] idex_shamt_4_0,
  output [1:0] idex_shift_op_1_0,
  output [31:0] idex_imm_ext_31_0,
  output [4:0] idex_rd_addr_4_0,
  output [31:0] idex_pc_31_0,
  output [31:0] idex_pc_4_31_0,
  output [2:0] idex_load_sel_2_0,
  output [2:0] idex_store_sel_2_0,
  output [31:0] idex_op_A_31_0,
  output [31:0] idex_op_B_31_0,
  output [4:0] idex_rs_addr_4_0,
  output [4:0] idex_rt_addr_4_0,
  output [4:0] idex_cp0_addr_4_0,
  output idex_cp0_w_en,
  output idex_syscall,
  output idex_eret,
  output ex_nop,
  output ex_jmp,
  output ex_jr,
  output out_71,
  output out_72,
  output out_73,
  output out_74,
  output out_75,
  output [3:0] idex_Md_op_3_0_2
);


  assign idex_movnz = 1'b1;
  assign idex_movz = 1'b1;
endmodule

module exmem_reg (
  input  clk,
  input  reset,
  input  cu_stall,
  input  cu_flush,
  input  idex_mem_w,
  input  idex_memr,
  input  idex_reg_w,
  input  idex_branch,
  input  [2:0] idex_condition_2_0,
  input  [31:0] adder_target_31_0,
  input  alu_lf,
  input  alu_zf,
  input  alu_of,
  input  [31:0] ex_res_31_0,
  input  [4:0] real_rd_addr_4_0,
  input  [2:0] idex_load_sel_2_0,
  input  [3:0] reg_byte_w_en_3_0,
  input  [3:0] mem_byte_w_en_3_0,
  input  [31:0] idex_pc_31_0,
  input  [31:0] idex_pc_4_31_0,
  input  [31:0] aligned_rt_data_31_0,
  input  [4:0] idex_cp0_dst_addr_4_0,
  input  cp0_w_en,
  input  syscall,
  input  idex_eret,
  input  ex_nop,
  input  ex_jmp,
  input  in_28,
  input  in_29,
  input  in_30,
  input  in_31,
  output [31:0] exmem_pc_31_0,
  output exmem_nen_w,
  output exmem_mem_r,
  output exmem_reg_w,
  output [3:0] reg_byte_w_en_3_0_2,
  output [4:0] exmem_rd_addr_4_0,
  output [3:0] mem_byte_w_en,
  output [31:0] exmem_alu_res_31_0,
  output [31:0] exmem_rt_data_31_0,
  output exmem_branch,
  output [2:0] exmem_condition_2_0,
  output [31:0] exmem_target_31_0,
  output [31:0] exmem_pc_4_31_0,
  output exmem_lf,
  output exmem_zf,
  output [2:0] exmem_load_sel_2_0,
  output [2:0] exmem_store_sel_2_0,
  output [4:0] exmem_cp0_dst_addr_4_0,
  output cp0_w_en_2,
  output syscall_2,
  output exmem_eret,
  output mem_nop,
  output mem_jmp,
  output out_55,
  output out_56,
  output out_57
);
endmodule

module memwb_reg (
  input  in_1,
  input  in_2,
  input  clk,
  input  reset,
  input  exmem_mem_r,
  input  exmem_mem_w,
  input  [3:0] reg_byte_w_en_3_0,
  input  [4:0] exmem_rd_addr_4_0,
  input  [31:0] mem_data_31_0,
  input  [31:0] ex_data_31_0,
  input  [4:0] exmem_cp0_dst_addr_4_0,
  input  exmem_cp0_w_en,
  input  [31:0] aligned_rt_data_31_0,
  output memwb_mem_r,
  output memwb_reg_w,
  output [4:0] memwb_rd_addr_4_0,
  output [3:0] reg_byte_w_en_3_0_2,
  output [31:0] memwb_memdata_31_0,
  output [31:0] memwb_exdata_31_0,
  output [4:0] memwb_cp0_dst_addr_4_0,
  output memwb_cp0_w_en,
  output [31:0] aligned_rt_data_31_0_2
);
endmodule

module ALU (
  input  [3:0] in_1,
  input  [31:0] in_2,
  input  [31:0] in_3,
  output [31:0] out_4,
  output out_5,
  output out_6,
  output out_7
);
endmodule

module lw_b_w_e_gen (
  input  [1:0] addr_1_0,
  input  [2:0] load_sel_2_0,
  output [3:0] b_w_en_3_0
);
endmodule

module sw_b_w_e_gen (
  input  [1:0] addr_1_0,
  input  [2:0] store_sel_2_0,
  output [3:0] b_w_en_3_0
);
endmodule

module real_rt_data_gen (
  input  [1:0] addr_1_0,
  input  [2:0] store_sel_2_0,
  input  [31:0] rt_data_31_0,
  output [31:0] real_rt_data_31_0
);
endmodule

module barrel_shifter (
  input  [4:0] shift_amount_4_0,
  input  [1:0] shift_op_1_0,
  input  [31:0] shift_in_31_0,
  output [31:0] shift_out_31_0
);
endmodule

module GPR (
  input  clk,
  input  reset,
  input  [4:0] Rs_addr_4_0,
  input  [4:0] Rt_addr_4_0,
  input  [31:0] data_in_31_0,
  input  write,
  input  [4:0] Rd_addr_4_0,
  input  [3:0] Rd_byte_w_en_3_0,
  output [31:0] Rs_data_31_0,
  output [31:0] Rt_data_31_0
);
endmodule

module mem_r_data_shift (
  input  [1:0] in_1,
  input  [2:0] in_2,
  input  [31:0] in_3,
  output [31:0] out_4
);
endmodule

module final_target (
  input  exmem_branch,
  input  [2:0] exmem_condition_2_0,
  input  [31:0] exmem_target_31_0,
  input  [31:0] exmem_pc_4_31_0,
  input  branch_state,
  input  exmem_lf,
  input  exmem_zf,
  output [31:0] final_target_31_0
);
endmodule

module pc (
  input  stall,
  input  clk,
  input  reset,
  input  [31:0] pc_in_31_0,
  output [31:0] pc_out_31_0
);
endmodule

module imm_ext (
  input  [15:0] ifid_imm_15_0,
  input  [1:0] id_imm_ext_1_0,
  output [31:0] imm_ext_31_0
);
endmodule

module control_unit (
  input  id_jr,
  input  mem_stall,
  input  id_jmp,
  input  exmem_syscall,
  input  idex_mem_r,
  input  [4:0] real_rs_addr_4_0,
  input  [4:0] real_rt_addr_4_0,
  input  [4:0] real_rd_addr_4_0,
  input  [31:0] preedicted_idex_pc_31_0,
  input  [31:0] target_exmem_pc_31_0,
  input  mem_branch_state,
  input  cp0_intr,
  input  exmem_eret,
  input  [31:0] in_14,
  output [2:0] cu_pc_src_2_0,
  output cu_pc_stall,
  output cu_ifid_stall,
  output cu_ifid_flush,
  output cu_idex_stall,
  output cu_idex_flush,
  output cu_exmem_stall,
  output cu_exmem_flush,
  output out_23,
  output out_24,
  output out_25,
  output out_26,
  output bpu_write_en,
  output out_28,
  output cu_cp0_w_en,
  output [4:0] cu_exec_code_4_0,
  output [31:0] cu_epc_321_0,
  output [31:0] cu_vector_31_0
);
endmodule

module forwarding_unit (
  input  [31:0] rs_data_31_0,
  input  [31:0] rt_data_31_0,
  input  [4:0] rs_addr,
  input  [4:0] rt_addr,
  input  [3:0] exmem_byte_en_3_0,
  input  [4:0] exmem_rd_addr,
  input  [3:0] memwb_byte_en_3_0,
  input  [4:0] memwb_rd_addr_4_0,
  input  [31:0] memwb_data_31_0,
  output [31:0] input_A_31_0,
  output [31:0] input_B_31_0,
  output [1:0] A_sel_1_0,
  output [1:0] B_sel_31_0
);
endmodule

module branch_predict_unit (
  input  [31:0] current_pc_31_0,
  input  [31:0] tag_pc_31_0,
  input  [31:0] next_pc_31_0,
  input  bpu_write_en,
  input  in_5,
  input  in_6,
  output [31:0] predicted_pc_31_0
);
endmodule

module cp0 (
  input  reset,
  input  clk,
  input  w_en_i,
  input  [4:0] w_addr_i_4_0,
  input  [31:0] data_in_31_0,
  input  [4:0] r_addr_i_4_0,
  input  [7:0] interruption_7_0,
  input  [31:0] excepttype_i_31_0,
  input  [31:0] current_inst_addr_i_31_0,
  input  is_in_delay_slot,
  output [31:0] data_o_31_0,
  output [31:0] status_o_31_0,
  output [31:0] cause_o_31_0,
  output [31:0] epc_o_31_0,
  output time_int_o
);
endmodule

module exception (
  input  in_1,
  input  [31:0] in_2,
  output out_3,
  output [4:0] out_4
);
endmodule

module pc_src_selector (
  input  [2:0] PC_SRC_2_0,
  input  [31:0] J_31_0,
  input  [31:0] JR_31_0,
  input  [31:0] VECTOR_31_0,
  input  [31:0] EPC_31_0,
  input  [31:0] TARGET_31_0,
  input  [31:0] BPU_31_0,
  output [31:0] PC_31_0
);
endmodule

module reg_w_gen (
  input  in_1,
  input  in_2,
  input  in_3,
  input  in_4,
  input  in_5,
  input  in_6,
  output out_7
);
endmodule

module cpu_interface (
  input  clk,
  input  reset,
  input  [29:0] ic_addr,
  input  dc_read_in,
  input  dc_write_in,
  input  [29:0] dc_addr,
  input  [31:0] data_reg,
  input  [3:0] dc_byte_w_en,
  output [31:0] ic_data_out,
  output [31:0] dc_data_out,
  output mem_stall
);
endmodule

module except_detect1 (
  input  in_1,
  input  in_2,
  input  in_3,
  output out_4
);
endmodule

module except_detect2 (
  input  in_1,
  input  in_2,
  input  in_3,
  input  in_4,
  input  in_5,
  input  in_6,
  input  [2:0] in_7,
  output out_8
);
endmodule

module is_delayslot (
  input  in_1,
  input  in_2,
  input  in_3,
  output out_4
);
endmodule

module muldiv (
  input  Clk,
  input  [3:0] Md_op_31_0,
  input  [31:0] Rs_in_31_0,
  input  [31:0] Rt_in_31_0,
  output [31:0] Res_out_31_0,
  output Md_stall
);
endmodule

module interrupt_except_handle (
  input  [31:0] in_1,
  input  [31:0] in_2,
  input  in_3,
  output [31:0] out_4
);
endmodule
