// Logisim project 流水线CPU框图_2016_1_10.circ as structural Verilog: 29 circuits, main circuit main
module main (
  input  [7:0] INTERRUPTIONS,
  input  CLK,
  input  RST,
  output ti
);

  wire alu_1_out_5, alu_1_out_6, alu_1_out_7, and_1_out, and_2_out, CONTROL_UNIT_cu_exmem_flush,
       CONTROL_UNIT_cu_exmem_stall, CONTROL_UNIT_cu_idex_flush, CONTROL_UNIT_cu_idex_stall,
       CONTROL_UNIT_cu_ifid_flush, CONTROL_UNIT_cu_ifid_stall, CONTROL_UNIT_cu_memwb_stall,
       CONTROL_UNIT_cu_pc_stall, cpu_interface_1_mem_stall, DECODER_p3, DECODER_p4, DECODER_p5, DECODER_p6,
       DECODER_p7, DECODER_p9, DECODER_p12, DECODER_p16, DECODER_p18, DECODER_p19, DECODER_p20, DECODER_p21,
       DECODER_p23, DECODER_p24, DECODER_p25, DECODER_p26, DECODER_p28, DECODER_p31,
       except_detect1_1_excepttype_31_0, except_detect2_1_excepttype_out_31_0, exmem_reg_1_cp0_w_en_2,
       exmem_reg_1_exmem_branch, exmem_reg_1_exmem_lf, exmem_reg_1_exmem_mem_r, exmem_reg_1_exmem_nen_w,
       exmem_reg_1_exmem_reg_w, exmem_reg_1_exmem_zf, exmem_reg_1_mem_jmp, exmem_reg_1_out_52,
       exmem_reg_1_out_53, IDEX_REG_ex_jmp, IDEX_REG_ex_jr, IDEX_REG_ex_nop, IDEX_REG_idex_b_sel,
       IDEX_REG_idex_branch, IDEX_REG_idex_cp0_w_en, IDEX_REG_idex_eret, IDEX_REG_idex_mem_r,
       IDEX_REG_idex_mem_w, IDEX_REG_idex_movnz, IDEX_REG_idex_movz, IDEX_REG_idex_of_w_disen,
       IDEX_REG_idex_reg_w, IDEX_REG_idex_shamt_sel, IDEX_REG_idex_syscall, IDEX_REG_out_70, IDEX_REG_out_71,
       IDEX_REG_out_72, IFID_REG_id_nop, interrupt_except_handle_1_out_5, interrupt_except_handle_1_out_6,
       memwb_reg_1_memwb_cp0_w_en, memwb_reg_1_memwb_mem_r, memwb_reg_1_memwb_reg_w, MUL_DIV_md_stall,
       not_1_out, not_2_out, or_1_out, or_2_out, or_3_out, reg_w_gen_1_out_7, undriven_2;
  wire [1:0] DECODER_p13, DECODER_p29, DECODER_p30, forwarding_unit_1_a_sel_1_0,
       forwarding_unit_1_b_sel_31_0, IDEX_REG_idex_exres_sel, IDEX_REG_idex_shift_op_1_0;
  wire [2:0] CONTROL_UNIT_cu_pc_src_2_0, DECODER_p8, DECODER_p10, DECODER_p14, DECODER_p15, DECODER_p22,
       exmem_reg_1_exmem_condition_2_0, exmem_reg_1_exmem_load_sel_2_0, IDEX_REG_idex_conition_2_0,
       IDEX_REG_idex_load_sel_2_0, IDEX_REG_idex_store_sel_2_0;
  wire [3:0] DECODER_p27, exmem_reg_1_mem_byte_w_en, exmem_reg_1_reg_byte_w_en_3_0_2,
       IDEX_REG_idex_alu_op_3_0, IDEX_REG_idex_md_op_3_0_2, LOAD_B_W_E_GEN_b_w_en_3_0,
       memwb_reg_1_reg_byte_w_en_3_0_2, STORE_B_W_E_GEN_b_w_en_3_0;
  wire [4:0] DECODER_p2, DECODER_p11, DECODER_p17, exmem_reg_1_exmem_cp0_dst_addr_4_0,
       exmem_reg_1_exmem_rd_addr_4_0, IDEX_REG_idex_cp0_addr_4_0, IDEX_REG_idex_rd_addr_4_0,
       IDEX_REG_idex_rs_addr_4_0, IDEX_REG_idex_rt_addr_4_0, IDEX_REG_idex_shamt_4_0,
       IFID_REG_ifid_rd_addr_4_0, IFID_REG_ifid_rs_addr_4_0, IFID_REG_ifid_rt_addr_4_0,
       memwb_reg_1_memwb_cp0_dst_addr_4_0, memwb_reg_1_memwb_rd_addr_4_0, multiplexer_2_out,
       multiplexer_4_out, multiplexer_9_out;
  wire [15:0] IFID_REG_ifid_imm_15_0;
  wire [31:0] adder_1_out, adder_2_out, alu_1_out_4, barrel_shifter_1_shift_out_31_0,
       CONTROL_UNIT_cu_vector_31_0, CP0_UNIT_cp0_v_cause_o_31_0, CP0_UNIT_cp0_v_data_o_31_0,
       CP0_UNIT_cp0_v_epc_o_31_0, CP0_UNIT_cp0_v_status_o_31_0, cpu_interface_1_dc_data_out,
       cpu_interface_1_ic_data_out, exmem_reg_1_exmem_alu_res_31_0, exmem_reg_1_exmem_pc_4_31_0,
       exmem_reg_1_exmem_pc_31_0, exmem_reg_1_exmem_rt_data_31_0, exmem_reg_1_exmem_target_31_0,
       EXTEND_Ext_unit_v_imm_ext_31_0, final_target_1_final_target_31_0, forwarding_unit_1_input_a_31_0,
       forwarding_unit_1_input_b_31_0, GPR_rs_data_31_0, GPR_rt_data_31_0, IDEX_REG_idex_imm_ext_31_0,
       IDEX_REG_idex_op_a_31_0, IDEX_REG_idex_op_b_31_0, IDEX_REG_idex_pc_4_31_0, IDEX_REG_idex_pc_31_0,
       IFID_REG_ifid_instr_31_0, IFID_REG_ifid_jump_instr_31_0, IFID_REG_ifid_pc_4_31_0,
       IFID_REG_ifid_pc_31_0, interrupt_except_handle_1_out_4, LOAD_SHIFTER_out_4,
       memwb_reg_1_memwb_exdata_31_0, memwb_reg_1_memwb_memdata_31_0, MUL_DIV_res_out_31_0,
       multiplexer_1_out, multiplexer_3_out, multiplexer_5_out, multiplexer_6_out, multiplexer_7_out,
       multiplexer_8_out, multiplexer_10_out, multiplexer_11_out, multiplexer_12_out, PC_pc_out_31_0,
       STORE_SHIFTER_real_rt_data_31_0, undriven;

  Multiplexer #(.select(3), .width(32), .disabled(0), .enable("false")) multiplexer_1 (
    .in0(IFID_REG_ifid_jump_instr_31_0), .in1(CONTROL_UNIT_cu_vector_31_0), .in2(CP0_UNIT_cp0_v_epc_o_31_0),
    .in3(final_target_1_final_target_31_0), .in4(adder_1_out), .out(multiplexer_1_out),
    .sel(CONTROL_UNIT_cu_pc_src_2_0));  // open: in5, in6, in7
  pc PC (
    .stall(CONTROL_UNIT_cu_pc_stall), .clk(CLK), .reset(RST), .pc_out_31_0(PC_pc_out_31_0),
    .pc_in_31_0(multiplexer_1_out));
  cpu_interface cpu_interface_1 (
    .clk(CLK), .reset(RST), .ic_addr(PC_pc_out_31_0[29:0]), .dc_read_in(and_2_out),
    .dc_write_in(exmem_reg_1_exmem_nen_w), .dc_addr(exmem_reg_1_exmem_alu_res_31_0[31:2]),
    .data_reg(exmem_reg_1_exmem_rt_data_31_0), .dc_byte_w_en(exmem_reg_1_mem_byte_w_en),
    .ic_data_out(cpu_interface_1_ic_data_out), .dc_data_out(cpu_interface_1_dc_data_out),
    .mem_stall(cpu_interface_1_mem_stall));
  ifid_reg IFID_REG (
    .clk(CLK), .reset(RST), .ifid_pc_31_0(IFID_REG_ifid_pc_31_0), .cu_stall(CONTROL_UNIT_cu_ifid_stall),
    .cu_flush(CONTROL_UNIT_cu_ifid_flush), .ifid_rs_addr_4_0(IFID_REG_ifid_rs_addr_4_0),
    .ifid_rt_addr_4_0(IFID_REG_ifid_rt_addr_4_0), .pc_31_0(PC_pc_out_31_0),
    .ifid_rd_addr_4_0(IFID_REG_ifid_rd_addr_4_0), .ifid_imm_15_0(IFID_REG_ifid_imm_15_0),
    .pc_4_31_0(adder_1_out), .ifid_pc_4_31_0(IFID_REG_ifid_pc_4_31_0),
    .instr_31_0(cpu_interface_1_ic_data_out), .ifid_jump_instr_31_0(IFID_REG_ifid_jump_instr_31_0),
    .ifid_instr_31_0(IFID_REG_ifid_instr_31_0), .id_nop(IFID_REG_id_nop));
  Adder #(.width(32)) adder_1 (.a(PC_pc_out_31_0), .b(32'h4), .out(adder_1_out));  // open: cin, cout
  or or_1 (or_1_out, cpu_interface_1_mem_stall, MUL_DIV_md_stall);
  // decoder DECODER: pin names not known; wires that end beside it: IFID_REG_ifid_instr_31_0, DECODER_p2, DECODER_p3, DECODER_p4, DECODER_p5, DECODER_p6, DECODER_p7, DECODER_p8, DECODER_p9, DECODER_p10, DECODER_p11, DECODER_p12, DECODER_p13, DECODER_p14, DECODER_p15, DECODER_p16, DECODER_p17, DECODER_p18, DECODER_p19, DECODER_p20, DECODER_p21, DECODER_p22, DECODER_p23, DECODER_p24, DECODER_p25, DECODER_p26, DECODER_p27, DECODER_p28, DECODER_p29, DECODER_p30, DECODER_p31
  GPR GPR (
    .clk(not_1_out), .reset(RST), .Rs_data_31_0(GPR_rs_data_31_0), .Rs_addr_4_0(IFID_REG_ifid_rs_addr_4_0),
    .Rt_addr_4_0(multiplexer_2_out), .Rd_addr_4_0(memwb_reg_1_memwb_rd_addr_4_0),
    .Rt_data_31_0(GPR_rt_data_31_0), .write(memwb_reg_1_memwb_reg_w), .data_in_31_0(multiplexer_12_out),
    .Rd_byte_w_en_3_0(memwb_reg_1_reg_byte_w_en_3_0_2));
  not not_1 (not_1_out, CLK);
  Multiplexer #(.width(5), .enable("false")) multiplexer_2 (
    .in0(IFID_REG_ifid_rt_addr_4_0), .in1({5{1'b0}}), .out(multiplexer_2_out), .sel(DECODER_p31));
  Multiplexer #(.width(32), .enable("false")) multiplexer_3 (
    .in0(CP0_UNIT_cp0_v_data_o_31_0), .in1(GPR_rt_data_31_0), .out(multiplexer_3_out), .sel(DECODER_p28));
  imm_ext EXTEND_Ext_unit_v (
    .ifid_imm_15_0(IFID_REG_ifid_imm_15_0), .imm_ext_31_0(EXTEND_Ext_unit_v_imm_ext_31_0),
    .id_imm_ext_1_0(DECODER_p29));
  except_detect1 except_detect1_1 (
    .syscall(DECODER_p19), .eret(DECODER_p20), .invalid_inst(DECODER_p26),
    .excepttype_31_0(except_detect1_1_excepttype_31_0));
  Multiplexer #(.select(2), .width(5), .enable("false")) multiplexer_4 (
    .in0(IFID_REG_ifid_rt_addr_4_0), .in1(IFID_REG_ifid_rd_addr_4_0), .in2({5{1'b1}}),
    .out(multiplexer_4_out), .sel(DECODER_p30));  // open: in3
  control_unit CONTROL_UNIT (
    .mem_stall(or_1_out), .cu_ifid_stall(CONTROL_UNIT_cu_ifid_stall), .id_jmp(DECODER_p3),
    .cu_ifid_flush(CONTROL_UNIT_cu_ifid_flush), .cu_idex_flush(CONTROL_UNIT_cu_idex_flush),
    .cu_pc_stall(CONTROL_UNIT_cu_pc_stall), .cu_idex_stall(CONTROL_UNIT_cu_idex_stall),
    .ifid_rs_addr_4_0(IFID_REG_ifid_rs_addr_4_0), .ifid_real_rd_addr_4_0(IDEX_REG_idex_rd_addr_4_0),
    .cu_exmem_stall(CONTROL_UNIT_cu_exmem_stall), .cu_exmem_flush(CONTROL_UNIT_cu_exmem_flush),
    .ifid_real_rt_addr_4_0(multiplexer_2_out), .cu_vector_31_0(CONTROL_UNIT_cu_vector_31_0),
    .cu_pc_src_2_0(CONTROL_UNIT_cu_pc_src_2_0), .mem_branch_state(undriven_2),
    .mem_excepttype(interrupt_except_handle_1_out_4), .cu_memwb_stall(CONTROL_UNIT_cu_memwb_stall),
    .reset(RST), .mem_jr(exmem_reg_1_mem_jmp));  // open: bpu_write_en
  idex_reg IDEX_REG (
    .idex_mem_w(IDEX_REG_idex_mem_w), .idex_mem_r(IDEX_REG_idex_mem_r), .clk(CLK),
    .idex_reg_w(IDEX_REG_idex_reg_w), .reset(RST), .idex_branch(IDEX_REG_idex_branch),
    .cu_stall(CONTROL_UNIT_cu_idex_stall), .idex_conition_2_0(IDEX_REG_idex_conition_2_0),
    .cu_flush(CONTROL_UNIT_cu_idex_flush), .idex_of_w_disen(IDEX_REG_idex_of_w_disen),
    .id_rd_addr_4_0(multiplexer_4_out), .idex_exres_sel(IDEX_REG_idex_exres_sel),
    .idex_B_sel(IDEX_REG_idex_b_sel), .idex_ALU_op_3_0(IDEX_REG_idex_alu_op_3_0),
    .ifid_pc_31_0(IFID_REG_ifid_pc_31_0), .idex_shamt_sel(IDEX_REG_idex_shamt_sel),
    .idex_shift_op_1_0(IDEX_REG_idex_shift_op_1_0), .idex_shamt_4_0(IDEX_REG_idex_shamt_4_0),
    .ifid_pc_4_31_0(IFID_REG_ifid_pc_4_31_0), .idex_rs_addr_4_0(IDEX_REG_idex_rs_addr_4_0),
    .idex_rt_addr_4_0(IDEX_REG_idex_rt_addr_4_0), .idex_rd_addr_4_0(IDEX_REG_idex_rd_addr_4_0),
    .gpr_rs_31_0(GPR_rs_data_31_0), .idex_op_A_31_0(IDEX_REG_idex_op_a_31_0),
    .gpr_rt_31_0(multiplexer_3_out), .idex_op_B_31_0(IDEX_REG_idex_op_b_31_0),
    .id_imm_ext_31_0(EXTEND_Ext_unit_v_imm_ext_31_0), .idex_imm_ext_31_0(IDEX_REG_idex_imm_ext_31_0),
    .idex_pc_31_0(IDEX_REG_idex_pc_31_0), .idex_pc_4_31_0(IDEX_REG_idex_pc_4_31_0),
    .idex_load_sel_2_0(IDEX_REG_idex_load_sel_2_0), .idex_store_sel_2_0(IDEX_REG_idex_store_sel_2_0),
    .idex_cp0_addr_4_0(IDEX_REG_idex_cp0_addr_4_0), .idex_syscall(IDEX_REG_idex_syscall),
    .idex_cp0_w_en(IDEX_REG_idex_cp0_w_en), .idex_eret(IDEX_REG_idex_eret), .idex_movz(IDEX_REG_idex_movz),
    .idex_movnz(IDEX_REG_idex_movnz), .in_13(DECODER_p4), .in_14(DECODER_p5), .in_15(DECODER_p6),
    .in_19(DECODER_p7), .in_24(DECODER_p8), .in_28(DECODER_p9), .in_16(DECODER_p10), .in_20(DECODER_p11),
    .in_25(DECODER_p12), .in_29(DECODER_p13), .in_32(DECODER_p14), .in_17(DECODER_p15), .in_21(DECODER_p16),
    .in_26(DECODER_p17), .in_30(DECODER_p18), .in_33(DECODER_p19), .in_18(DECODER_p20), .in_22(DECODER_p21),
    .in_27(DECODER_p22), .in_31(DECODER_p23), .in_34(DECODER_p24), .in_12(IFID_REG_id_nop),
    .in_11(DECODER_p3), .ex_nop(IDEX_REG_ex_nop), .ex_jmp(IDEX_REG_ex_jmp), .ex_jr(IDEX_REG_ex_jr),
    .in_23(except_detect1_1_excepttype_31_0), .in_35(DECODER_p25), .out_72(IDEX_REG_out_72),
    .out_70(IDEX_REG_out_70), .out_71(IDEX_REG_out_71), .in_37(or_3_out), .idex_Md_op_3_0(DECODER_p27),
    .idex_Md_op_3_0_2(IDEX_REG_idex_md_op_3_0_2));  // open: in_36
  or or_2 (or_2_out, IDEX_REG_idex_movz, IDEX_REG_idex_movnz);
  or or_3 (or_3_out, IDEX_REG_ex_jmp, IDEX_REG_ex_jr, IDEX_REG_idex_branch);
  forwarding_unit forwarding_unit_1 (
    .rs_data_31_0(IDEX_REG_idex_op_a_31_0), .rt_data_31_0(IDEX_REG_idex_op_b_31_0),
    .memwb_byte_en_3_0(memwb_reg_1_reg_byte_w_en_3_0_2), .rs_addr(IDEX_REG_idex_rs_addr_4_0),
    .rt_addr(IDEX_REG_idex_rt_addr_4_0), .memwb_rd_addr_4_0(memwb_reg_1_memwb_rd_addr_4_0),
    .input_A_31_0(forwarding_unit_1_input_a_31_0), .input_B_31_0(forwarding_unit_1_input_b_31_0),
    .A_sel_1_0(forwarding_unit_1_a_sel_1_0), .memwb_data_31_0(multiplexer_12_out),
    .B_sel_31_0(forwarding_unit_1_b_sel_31_0), .exmem_rd_addr(exmem_reg_1_exmem_rd_addr_4_0),
    .exmem_byte_en_3_0(exmem_reg_1_reg_byte_w_en_3_0_2));
  Multiplexer #(.select(2), .width(32), .enable("false")) multiplexer_5 (
    .in0(IDEX_REG_idex_op_a_31_0), .in1(exmem_reg_1_exmem_alu_res_31_0),
    .in2(forwarding_unit_1_input_a_31_0), .out(multiplexer_5_out), .sel(forwarding_unit_1_a_sel_1_0));  // open: in3
  Multiplexer #(.select(2), .width(32), .enable("false")) multiplexer_6 (
    .in0(IDEX_REG_idex_op_b_31_0), .in1(exmem_reg_1_exmem_alu_res_31_0),
    .in2(forwarding_unit_1_input_b_31_0), .out(multiplexer_6_out), .sel(forwarding_unit_1_b_sel_31_0));  // open: in3
  Multiplexer #(.width(32), .enable("false")) multiplexer_7 (
    .in0(multiplexer_5_out), .in1(undriven), .out(multiplexer_7_out), .sel(or_2_out));
  Multiplexer #(.width(32), .enable("false")) multiplexer_8 (
    .in0(multiplexer_6_out), .in1(IDEX_REG_idex_imm_ext_31_0), .out(multiplexer_8_out),
    .sel(IDEX_REG_idex_b_sel));
  Multiplexer #(.width(5), .enable("false")) multiplexer_9 (
    .in0(IDEX_REG_idex_shamt_4_0), .in1(multiplexer_5_out[4:0]), .out(multiplexer_9_out),
    .sel(IDEX_REG_idex_shamt_sel));
  except_detect2 except_detect2_1 (
    .\if (alu_1_out_5), .of(alu_1_out_6), .zf(alu_1_out_7), .trap(IDEX_REG_out_71),
    .overflow_detect(IDEX_REG_idex_of_w_disen), .excepttype_in_31_0(IDEX_REG_out_72),
    .excepttype_out_31_0(except_detect2_1_excepttype_out_31_0), .condition_2_0(IDEX_REG_idex_conition_2_0));
  muldiv MUL_DIV (
    .Clk(CLK), .Md_op_31_0(IDEX_REG_idex_md_op_3_0_2), .Rs_in_31_0(multiplexer_7_out),
    .Rt_in_31_0(multiplexer_8_out), .Res_out_31_0(MUL_DIV_res_out_31_0), .Md_stall(MUL_DIV_md_stall));
  ALU alu_1 (
    .in_2(multiplexer_7_out), .in_3(multiplexer_8_out), .in_1(IDEX_REG_idex_alu_op_3_0), .out_4(alu_1_out_4),
    .out_5(alu_1_out_5), .out_6(alu_1_out_6), .out_7(alu_1_out_7));
  barrel_shifter barrel_shifter_1 (
    .shift_amount_4_0(multiplexer_9_out), .shift_op_1_0(IDEX_REG_idex_shift_op_1_0),
    .shift_in_31_0(multiplexer_6_out), .shift_out_31_0(barrel_shifter_1_shift_out_31_0));
  reg_w_gen reg_w_gen_1 (
    .in_3(IDEX_REG_idex_movz), .in_4(IDEX_REG_idex_movnz), .in_5(IDEX_REG_idex_reg_w),
    .in_6(IDEX_REG_idex_of_w_disen), .out_7(reg_w_gen_1_out_7), .in_1(alu_1_out_7), .in_2(alu_1_out_6));
  Adder #(.width(32)) adder_2 (
    .a({IDEX_REG_idex_imm_ext_31_0[29:0], 2'b00}), .b(IDEX_REG_idex_pc_4_31_0), .out(adder_2_out));  // open: cin, cout
  Multiplexer #(.width(32), .disabled(0), .enable("false")) multiplexer_10 (
    .in0(adder_2_out), .in1(alu_1_out_4), .out(multiplexer_10_out), .sel(IDEX_REG_ex_jr));
  lw_b_w_e_gen LOAD_B_W_E_GEN (
    .addr_1_0(alu_1_out_4[1:0]), .load_sel_2_0(IDEX_REG_idex_load_sel_2_0),
    .b_w_en_3_0(LOAD_B_W_E_GEN_b_w_en_3_0));
  sw_b_w_e_gen STORE_B_W_E_GEN (
    .addr_1_0(alu_1_out_4[1:0]), .store_sel_2_0(IDEX_REG_idex_store_sel_2_0),
    .b_w_en_3_0(STORE_B_W_E_GEN_b_w_en_3_0));
  real_rt_data_gen STORE_SHIFTER (
    .addr_1_0(alu_1_out_4[1:0]), .store_sel_2_0(IDEX_REG_idex_store_sel_2_0),
    .rt_data_31_0(multiplexer_6_out), .real_rt_data_31_0(STORE_SHIFTER_real_rt_data_31_0));
  Multiplexer #(.select(2), .width(32), .enable("false")) multiplexer_11 (
    .in0(alu_1_out_4), .in1(barrel_shifter_1_shift_out_31_0), .in2(multiplexer_10_out),
    .in3(multiplexer_5_out), .out(multiplexer_11_out), .sel(IDEX_REG_idex_exres_sel));
  exmem_reg exmem_reg_1 (
    .clk(CLK), .idex_branch(IDEX_REG_idex_branch), .reset(RST),
    .idex_condition_2_0(IDEX_REG_idex_conition_2_0), .cu_stall(CONTROL_UNIT_cu_exmem_stall),
    .cu_flush(CONTROL_UNIT_cu_exmem_flush), .adder_target_31_0(multiplexer_10_out),
    .idex_mem_w(IDEX_REG_idex_mem_w), .idex_pc_31_0(IDEX_REG_idex_pc_31_0), .idex_memr(IDEX_REG_idex_mem_r),
    .idex_pc_4_31_0(IDEX_REG_idex_pc_4_31_0), .alu_lf(alu_1_out_5), .alu_zf(alu_1_out_6),
    .aligned_rt_data_31_0(STORE_SHIFTER_real_rt_data_31_0), .ex_res_31_0(multiplexer_11_out),
    .real_rd_addr_4_0(IDEX_REG_idex_rd_addr_4_0), .idex_load_sel_2_0(IDEX_REG_idex_load_sel_2_0),
    .exmem_nen_w(exmem_reg_1_exmem_nen_w), .exmem_mem_r(exmem_reg_1_exmem_mem_r),
    .exmem_reg_w(exmem_reg_1_exmem_reg_w), .exmem_condition_2_0(exmem_reg_1_exmem_condition_2_0),
    .exmem_branch(exmem_reg_1_exmem_branch), .exmem_alu_res_31_0(exmem_reg_1_exmem_alu_res_31_0),
    .exmem_rt_data_31_0(exmem_reg_1_exmem_rt_data_31_0), .exmem_target_31_0(exmem_reg_1_exmem_target_31_0),
    .exmem_lf(exmem_reg_1_exmem_lf), .exmem_zf(exmem_reg_1_exmem_zf),
    .exmem_pc_31_0(exmem_reg_1_exmem_pc_31_0), .exmem_pc_4_31_0(exmem_reg_1_exmem_pc_4_31_0),
    .exmem_rd_addr_4_0(exmem_reg_1_exmem_rd_addr_4_0), .exmem_load_sel_2_0(exmem_reg_1_exmem_load_sel_2_0),
    .reg_byte_w_en_3_0(LOAD_B_W_E_GEN_b_w_en_3_0), .mem_byte_w_en_3_0(STORE_B_W_E_GEN_b_w_en_3_0),
    .reg_byte_w_en_3_0_2(exmem_reg_1_reg_byte_w_en_3_0_2), .mem_byte_w_en(exmem_reg_1_mem_byte_w_en),
    .idex_cp0_dst_addr_4_0(IDEX_REG_idex_cp0_addr_4_0), .cp0_w_en(IDEX_REG_idex_cp0_w_en),
    .syscall(IDEX_REG_idex_syscall), .exmem_cp0_dst_addr_4_0(exmem_reg_1_exmem_cp0_dst_addr_4_0),
    .cp0_w_en_2(exmem_reg_1_cp0_w_en_2), .idex_eret(IDEX_REG_idex_eret), .alu_of(alu_1_out_7),
    .idex_reg_w(reg_w_gen_1_out_7), .ex_nop(IDEX_REG_ex_nop), .ex_jmp(IDEX_REG_ex_jmp),
    .mem_jmp(exmem_reg_1_mem_jmp), .in_28(IDEX_REG_out_70), .in_30(except_detect2_1_excepttype_out_31_0),
    .out_52(exmem_reg_1_out_52), .out_53(exmem_reg_1_out_53), .in_29(IDEX_REG_ex_jr));  // open: syscall_2, exmem_eret
  not not_2 (not_2_out, CLK);
  cp0 CP0_UNIT_cp0_v (
    .w_addr_i_4_0(memwb_reg_1_memwb_cp0_dst_addr_4_0), .is_in_delay_slot(exmem_reg_1_out_52),
    .data_in_31_0(multiplexer_12_out), .excepttype_i_31_0(interrupt_except_handle_1_out_4),
    .data_o_31_0(CP0_UNIT_cp0_v_data_o_31_0), .status_o_31_0(CP0_UNIT_cp0_v_status_o_31_0),
    .interruption_7_0(INTERRUPTIONS), .r_addr_i_4_0(DECODER_p2),
    .current_inst_addr_i_31_0(exmem_reg_1_exmem_pc_31_0), .cause_o_31_0(CP0_UNIT_cp0_v_cause_o_31_0),
    .epc_o_31_0(CP0_UNIT_cp0_v_epc_o_31_0), .time_int_o(ti), .w_en_i(memwb_reg_1_memwb_cp0_w_en),
    .clk(not_2_out), .reset(RST));
  interrupt_except_handle interrupt_except_handle_1 (
    .in_1(CP0_UNIT_cp0_v_status_o_31_0), .in_2(CP0_UNIT_cp0_v_cause_o_31_0), .in_3(exmem_reg_1_out_53),
    .out_4(interrupt_except_handle_1_out_4), .out_5(interrupt_except_handle_1_out_5),
    .out_6(interrupt_except_handle_1_out_6));
  final_target final_target_1 (
    .exmem_branch(exmem_reg_1_exmem_branch), .exmem_condition_2_0(exmem_reg_1_exmem_condition_2_0),
    .exmem_lf(exmem_reg_1_exmem_lf), .exmem_zf(exmem_reg_1_exmem_zf),
    .exmem_target_31_0(exmem_reg_1_exmem_target_31_0), .exmem_pc_4_31_0(exmem_reg_1_exmem_pc_4_31_0),
    .final_target_31_0(final_target_1_final_target_31_0), .branch_state(undriven_2));
  mem_r_data_shift LOAD_SHIFTER (
    .in_1(exmem_reg_1_exmem_alu_res_31_0[1:0]), .in_2(exmem_reg_1_exmem_load_sel_2_0),
    .in_3(cpu_interface_1_dc_data_out), .out_4(LOAD_SHIFTER_out_4));
  and and_1 (and_1_out, interrupt_except_handle_1_out_5, exmem_reg_1_exmem_reg_w);
  and and_2 (and_2_out, interrupt_except_handle_1_out_6, exmem_reg_1_exmem_mem_r);
  memwb_reg memwb_reg_1 (
    .clk(CLK), .reset(RST), .exmem_mem_r(and_2_out), .exmem_mem_w(and_1_out),
    .exmem_rd_addr_4_0(exmem_reg_1_exmem_rd_addr_4_0), .reg_byte_w_en_3_0(exmem_reg_1_reg_byte_w_en_3_0_2),
    .mem_data_31_0(LOAD_SHIFTER_out_4), .ex_data_31_0(exmem_reg_1_exmem_alu_res_31_0),
    .memwb_mem_r(memwb_reg_1_memwb_mem_r), .memwb_reg_w(memwb_reg_1_memwb_reg_w),
    .memwb_rd_addr_4_0(memwb_reg_1_memwb_rd_addr_4_0), .reg_byte_w_en_3_0_2(memwb_reg_1_reg_byte_w_en_3_0_2),
    .memwb_exdata_31_0(memwb_reg_1_memwb_exdata_31_0), .memwb_memdata_31_0(memwb_reg_1_memwb_memdata_31_0),
    .exmem_cp0_dst_addr_4_0(exmem_reg_1_exmem_cp0_dst_addr_4_0), .exmem_cp0_w_en(exmem_reg_1_cp0_w_en_2),
    .memwb_cp0_dst_addr_4_0(memwb_reg_1_memwb_cp0_dst_addr_4_0), .memwb_cp0_w_en(memwb_reg_1_memwb_cp0_w_en),
    .aligned_rt_data_31_0(exmem_reg_1_exmem_rt_data_31_0), .in_1(CONTROL_UNIT_cu_memwb_stall));  // open: aligned_rt_data_31_0_2
  Multiplexer #(.width(32), .enable("false")) multiplexer_12 (
    .in0(memwb_reg_1_memwb_exdata_31_0), .in1(memwb_reg_1_memwb_memdata_31_0), .out(multiplexer_12_out),
    .sel(memwb_reg_1_memwb_mem_r));

  // Notes on the sheet:
  //   M1
  //   A1
  //   CACHE
  //   M2
  //   byte_en
  //   addr
  //   write
  //   data
  //   M3
  //   EXCEPT_DETECT1
  //   Rd_addr_sel
  //   M4
  //   o1
  //   is_delayslot
  //   FORWARD_UNIT(FU.v)
  //   new_reg_w = ((movnz && zf) || (movz && !zf) || (id_of_w_disen && of)) ? 0 : idex_reg_w
  //   32'd0
  //   M5
  //   M6
  //   M7
  //   Rt_imm_sel
  //   M8
  //   shift_amount_sel
  //   M9
  //   EXCEPT_DETECT2
  //   ALU
  //   BARREL_SHIFTER(SHIFT.v)
  //   NEW_RW(reg_w_gen.v)
  //   A2
  //   M10
  //   Exec_res_sel
  //   M11
  //   EXMEM_REG
  //   IEH(interrupt_except_handle.v)
  //   BRANCH_ADDR(final_target.v)
  //   AND0
  //   AND1
  //   MEMWB_REG
  //   M12
endmodule

module ifid_reg (
  input  clk,
  input  reset,
  input  cu_stall,
  input  cu_flush,
  input  [31:0] pc_31_0,
  input  [31:0] pc_4_31_0,
  input  [31:0] instr_31_0,
  output [31:0] ifid_pc_31_0,
  output [31:0] ifid_pc_4_31_0,
  output [31:0] ifid_jump_instr_31_0,
  output [31:0] ifid_instr_31_0,
  output [4:0] ifid_rs_addr_4_0,
  output [4:0] ifid_rt_addr_4_0,
  output [15:0] ifid_imm_15_0,
  output [4:0] ifid_rd_addr_4_0,
  output id_nop
);
endmodule

module decoder (
  input  [31:0] ifid_instr_31_0,
  output out_2,
  output out_3,
  output out_4,
  output [2:0] out_5,
  output out_6,
  output out_7,
  output [2:0] out_8,
  output [4:0] out_9,
  output out_10,
  output [1:0] out_11,
  output [2:0] out_12,
  output [2:0] out_13,
  output out_14,
  output [4:0] out_15,
  output out_16,
  output out_17,
  output out_18,
  output out_19,
  output [2:0] out_20,
  output out_21,
  output out_22,
  output [4:0] cp0_src_addr_3_0,
  output id_rt_data_sel,
  output [1:0] id_rd_addr_sel_1_0,
  output id_jump,
  output out_27,
  output [1:0] in_imm_ext_1_0,
  output id_rt_addr_sel,
  output out_30,
  output [3:0] idex_Md_op
);
endmodule

module idex_reg (
  input  clk,
  input  reset,
  input  cu_stall,
  input  cu_flush,
  input  [4:0] id_rd_addr_4_0,
  input  [31:0] ifid_pc_31_0,
  input  [31:0] ifid_pc_4_31_0,
  input  [31:0] gpr_rs_31_0,
  input  [31:0] gpr_rt_31_0,
  input  [31:0] id_imm_ext_31_0,
  input  in_11,
  input  in_12,
  input  in_13,
  input  in_14,
  input  in_15,
  input  [2:0] in_16,
  input  [2:0] in_17,
  input  in_18,
  input  in_19,
  input  [4:0] in_20,
  input  in_21,
  input  in_22,
  input  in_23,
  input  [2:0] in_24,
  input  in_25,
  input  [4:0] in_26,
  input  [2:0] in_27,
  input  in_28,
  input  [1:0] in_29,
  input  in_30,
  input  in_31,
  input  [2:0] in_32,
  input  in_33,
  input  in_34,
  input  in_35,
  input  in_36,
  input  in_37,
  input  [3:0] idex_Md_op_3_0,
  output idex_movz,
  output idex_movnz,
  output idex_mem_w,
  output idex_mem_r,
  output idex_reg_w,
  output idex_branch,
  output [2:0] idex_conition_2_0,
  output idex_of_w_disen,
  output [1:0] idex_exres_sel,
  output idex_B_sel,
  output [3:0] idex_ALU_op_3_0,
  output idex_shamt_sel,
  output [4:0] idex_shamt_4_0,
  output [1:0] idex_shift_op_1_0,
  output [31:0] idex_imm_ext_31_0,
  output [4:0] idex_rd_addr_4_0,
  output [31:0] idex_pc_31_0,
  output [31:0] idex_pc_4_31_0,
  output [2:0] idex_load_sel_2_0,
  output [2:0] idex_store_sel_2_0,
  output [31:0] idex_op_A_31_0,
  output [31:0] idex_op_B_31_0,
  output [4:0] idex_rs_addr_4_0,
  output [4:0] idex_rt_addr_4_0,
  output [4:0] idex_cp0_addr_4_0,
  output idex_cp0_w_en,
  output idex_syscall,
  output idex_eret,
  output ex_nop,
  output ex_jmp,
  output ex_jr,
  output out_70,
  output out_71,
  output out_72,
  output [3:0] idex_Md_op_3_0_2
);


  assign idex_movnz = 1'b1;
  assign idex_movz = 1'b1;
endmodule

module exmem_reg (
  input  clk,
  input  reset,
  input  cu_stall,
  input  cu_flush,
  input  idex_mem_w,
  input  idex_memr,
  input  idex_reg_w,
  input  idex_branch,
  input  [2:0] idex_condition_2_0,
  input  [31:0] adder_target_31_0,
  input  alu_lf,
  input  alu_zf,
  input  alu_of,
  input  [31:0] ex_res_31_0,
  input  [4:0] real_rd_addr_4_0,
  input  [2:0] idex_load_sel_2_0,
  input  [3:0] reg_byte_w_en_3_0,
  input  [3:0] mem_byte_w_en_3_0,
  input  [31:0] idex_pc_31_0,
  input  [31:0] idex_pc_4_31_0,
  input  [31:0] aligned_rt_data_31_0,
  input  [4:0] idex_cp0_dst_addr_4_0,
  input  cp0_w_en,
  input  syscall,
  input  idex_eret,
  input  ex_nop,
  input  ex_jmp,
  input  in_28,
  input  in_29,
  input  in_30,
  output [31:0] exmem_pc_31_0,
  output exmem_nen_w,
  output exmem_mem_r,
  output exmem_reg_w,
  output [3:0] reg_byte_w_en_3_0_2,
  output [4:0] exmem_rd_addr_4_0,
  output [3:0] mem_byte_w_en,
  output [31:0] exmem_alu_res_31_0,
  output [31:0] exmem_rt_data_31_0,
  output exmem_branch,
  output [2:0] exmem_condition_2_0,
  output [31:0] exmem_target_31_0,
  output [31:0] exmem_pc_4_31_0,
  output exmem_lf,
  output exmem_zf,
  output [2:0] exmem_load_sel_2_0,
  output [4:0] exmem_cp0_dst_addr_4_0,
  output cp0_w_en_2,
  output syscall_2,
  output exmem_eret,
  output mem_jmp,
  output out_52,
  output out_53
);
endmodule

module memwb_reg (
  input  in_1,
  input  clk,
  input  reset,
  input  exmem_mem_r,
  input  exmem_mem_w,
  input  [3:0] reg_byte_w_en_3_0,
  input  [4:0] exmem_rd_addr_4_0,
  input  [31:0] mem_data_31_0,
  input  [31:0] ex_data_31_0,
  input  [4:0] exmem_cp0_dst_addr_4_0,
  input  exmem_cp0_w_en,
  input  [31:0] aligned_rt_data_31_0,
  output memwb_mem_r,
  output memwb_reg_w,
  output [4:0] memwb_rd_addr_4_0,
  output [3:0] reg_byte_w_en_3_0_2,
  output [31:0] memwb_exdata_31_0,
  output [31:0] memwb_memdata_31_0,
  output [4:0] memwb_cp0_dst_addr_4_0,
  output memwb_cp0_w_en,
  output [31:0] aligned_rt_data_31_0_2
);
endmodule

module ALU (
  input  [3:0] in_1,
  input  [31:0] in_2,
  input  [31:0] in_3,
  output [31:0] out_4,
  output out_5,
  output out_6,
  output out_7
);
endmodule

module lw_b_w_e_gen (
  input  [1:0] addr_1_0,
  input  [2:0] load_sel_2_0,
  output [3:0] b_w_en_3_0
);
endmodule

module sw_b_w_e_gen (
  input  [1:0] addr_1_0,
  input  [2:0] store_sel_2_0,
  output [3:0] b_w_en_3_0
);
endmodule

module real_rt_data_gen (
  input  [1:0] addr_1_0,
  input  [2:0] store_sel_2_0,
  input  [31:0] rt_data_31_0,
  output [31:0] real_rt_data_31_0
);
endmodule

module barrel_shifter (
  input  [4:0] shift_amount_4_0,
  input  [1:0] shift_op_1_0,
  input  [31:0] shift_in_31_0,
  output [31:0] shift_out_31_0
);
endmodule

module GPR (
  input  clk,
  input  reset,
  input  [4:0] Rs_addr_4_0,
  input  [4:0] Rt_addr_4_0,
  input  [31:0] data_in_31_0,
  input  write,
  input  [4:0] Rd_addr_4_0,
  input  [3:0] Rd_byte_w_en_3_0,
  output [31:0] Rs_data_31_0,
  output [31:0] Rt_data_31_0
);
endmodule

module mem_r_data_shift (
  input  [1:0] in_1,
  input  [2:0] in_2,
  input  [31:0] in_3,
  output [31:0] out_4
);
endmodule

module final_target (
  input  exmem_branch,
  input  [2:0] exmem_condition_2_0,
  input  [31:0] exmem_target_31_0,
  input  [31:0] exmem_pc_4_31_0,
  input  branch_state,
  input  exmem_lf,
  input  exmem_zf,
  output [31:0] final_target_31_0
);
endmodule

module pc (
  input  stall,
  input  clk,
  input  reset,
  input  [31:0] pc_in_31_0,
  output [31:0] pc_out_31_0
);
endmodule

module imm_ext (
  input  [15:0] ifid_imm_15_0,
  input  [1:0] id_imm_ext_1_0,
  output [31:0] imm_ext_31_0
);
endmodule

module control_unit (
  input  reset,
  input  mem_jr,
  input  mem_stall,
  input  id_jmp,
  input  [4:0] ifid_rs_addr_4_0,
  input  [4:0] ifid_real_rt_addr_4_0,
  input  [4:0] ifid_real_rd_addr_4_0,
  input  mem_branch_state,
  input  [31:0] mem_excepttype,
  output [2:0] cu_pc_src_2_0,
  output cu_pc_stall,
  output cu_ifid_stall,
  output cu_ifid_flush,
  output cu_idex_stall,
  output cu_idex_flush,
  output cu_exmem_stall,
  output cu_exmem_flush,
  output cu_memwb_stall,
  output bpu_write_en,
  output [31:0] cu_vector_31_0
);
endmodule

module forwarding_unit (
  input  [31:0] rs_data_31_0,
  input  [31:0] rt_data_31_0,
  input  [4:0] rs_addr,
  input  [4:0] rt_addr,
  input  [3:0] exmem_byte_en_3_0,
  input  [4:0] exmem_rd_addr,
  input  [3:0] memwb_byte_en_3_0,
  input  [4:0] memwb_rd_addr_4_0,
  input  [31:0] memwb_data_31_0,
  output [31:0] input_A_31_0,
  output [31:0] input_B_31_0,
  output [1:0] A_sel_1_0,
  output [1:0] B_sel_31_0
);
endmodule

module branch_predict_unit (
  input  [31:0] current_pc_31_0,
  input  [31:0] tag_pc_31_0,
  input  [31:0] next_pc_31_0,
  input  bpu_write_en,
  input  in_5,
  input  in_6,
  output [31:0] predicted_pc_31_0
);
endmodule

module cp0 (
  input  reset,
  input  clk,
  input  w_en_i,
  input  [4:0] w_addr_i_4_0,
  input  [31:0] data_in_31_0,
  input  [4:0] r_addr_i_4_0,
  input  [7:0] interruption_7_0,
  input  [31:0] excepttype_i_31_0,
  input  [31:0] current_inst_addr_i_31_0,
  input  is_in_delay_slot,
  output [31:0] data_o_31_0,
  output [31:0] status_o_31_0,
  output [31:0] cause_o_31_0,
  output [31:0] epc_o_31_0,
  output time_int_o
);
endmodule

module exception (
  input  in_1,
  input  [31:0] in_2,
  output out_3,
  output [4:0] out_4
);
endmodule

module pc_src_selector (
  input  [2:0] PC_SRC_2_0,
  input  [31:0] J_31_0,
  input  [31:0] JR_31_0,
  input  [31:0] VECTOR_31_0,
  input  [31:0] EPC_31_0,
  input  [31:0] TARGET_31_0,
  input  [31:0] BPU_31_0,
  output [31:0] PC_31_0
);
endmodule

module reg_w_gen (
  input  in_1,
  input  in_2,
  input  in_3,
  input  in_4,
  input  in_5,
  input  in_6,
  output out_7
);
endmodule

module cpu_interface (
  input  clk,
  input  reset,
  input  [29:0] ic_addr,
  input  dc_read_in,
  input  dc_write_in,
  input  [29:0] dc_addr,
  input  [31:0] data_reg,
  input  [3:0] dc_byte_w_en,
  output [31:0] ic_data_out,
  output [31:0] dc_data_out,
  output mem_stall
);
endmodule

module except_detect1 (
  input  syscall,
  input  eret,
  input  invalid_inst,
  output excepttype_31_0
);
endmodule

module except_detect2 (
  input  \if ,
  input  of,
  input  zf,
  input  [2:0] condition_2_0,
  input  trap,
  input  overflow_detect,
  input  excepttype_in_31_0,
  output excepttype_out_31_0
);
endmodule

module is_delayslot (
  input  in_1,
  input  in_2,
  input  in_3,
  output out_4
);
endmodule

module muldiv (
  input  Clk,
  input  [3:0] Md_op_31_0,
  input  [31:0] Rs_in_31_0,
  input  [31:0] Rt_in_31_0,
  output [31:0] Res_out_31_0,
  output Md_stall
);
endmodule

module interrupt_except_handle (
  input  [31:0] in_1,
  input  [31:0] in_2,
  input  in_3,
  output [31:0] out_4,
  output out_5,
  output out_6
);
endmodule
